# Fritzing sketch wiring (saved by Fritzing 0.9.4)
circuit board: 14.245cm x 7.34243cm

parts:
  S1 = Cherry MX Keyswitch
  S2 = Cherry MX Keyswitch
  D1 = Diode [package=diode-1n4148]
  D2 = Diode [package=diode-1n4148]
  D4 = Diode [package=diode-1n4148]
  D5 = Diode [package=diode-1n4148]
  S3 = Cherry MX Keyswitch
  S4 = Cherry MX Keyswitch
  S5 = Cherry MX Keyswitch
  D6 = Diode [package=diode-1n4148]
  S6 = Cherry MX Keyswitch
  S7 = Cherry MX Keyswitch
  S8 = Cherry MX Keyswitch
  S9 = Cherry MX Keyswitch
  S10 = Cherry MX Keyswitch
  D7 = Diode [package=diode-1n4148]
  D8 = Diode [package=diode-1n4148]
  D9 = Diode [package=diode-1n4148]
  D10 = Diode [package=diode-1n4148]
  D11 = Diode [package=diode-1n4148]
  S11 = Cherry MX Keyswitch
  S12 = Cherry MX Keyswitch
  S13 = Cherry MX Keyswitch
  S14 = Cherry MX Keyswitch
  S15 = Cherry MX Keyswitch
  D12 = Diode [package=diode-1n4148]
  D13 = Diode [package=diode-1n4148]
  D14 = Diode [package=diode-1n4148]
  D15 = Diode [package=diode-1n4148]
  D16 = Diode [package=diode-1n4148]
  S16 = Cherry MX Keyswitch
  S17 = Cherry MX Keyswitch
  S18 = Cherry MX Keyswitch
  S19 = Cherry MX Keyswitch
  S20 = Cherry MX Keyswitch
  D17 = Diode [package=diode-1n4148]
  D18 = Diode [package=diode-1n4148]
  D19 = Diode [package=diode-1n4148]
  D20 = Diode [package=diode-1n4148]
  D21 = Diode [package=diode-1n4148]
  Pro_Micro1 = SparkFun Pro Micro
  Grove1 = Grove OLED 128x96

nets:
  N1: S1.pin_3, D1.A
  N2: S1.pin_5, S8.pin_5, S13.pin_5, S18.pin_5
  N3: S2.pin_3, D2.A
  N4: S2.pin_5, S10.pin_5, S15.pin_5, S20.pin_5, Pro_Micro1.6
  N5: D1.C, D2.C, D4.C, D5.C, D6.C, Pro_Micro1.15, Pro_Micro1.A0
  N6: D4.A, S3.pin_3
  N7: D5.A, S4.pin_3
  N8: S3.pin_5, S7.pin_5, S12.pin_5, S17.pin_5, Pro_Micro1.7
  N9: S4.pin_5, S6.pin_5, S11.pin_5, S16.pin_5, Pro_Micro1.8
  N10: S5.pin_3, D6.A
  N11: S5.pin_5, S9.pin_5, S14.pin_5, S19.pin_5, Pro_Micro1.9
  N12: S6.pin_3, D7.A
  N13: S7.pin_3, D8.A
  N14: S8.pin_3, D11.A
  N15: S9.pin_3, D9.A
  N16: S10.pin_3, D10.A
  N17: D7.C, D8.C, D9.C, D10.C, D11.C, Pro_Micro1.14
  N18: S11.pin_3, D12.A
  N19: S12.pin_3, D13.A
  N20: S13.pin_3, D16.A
  N21: S14.pin_3, D14.A
  N22: S15.pin_3, D15.A
  N23: D12.C, D13.C, D14.C, D15.C, D16.C, Pro_Micro1.16
  N24: S16.pin_3, D17.A
  N25: S17.pin_3, D18.A
  N26: S18.pin_3, D21.A
  N27: S19.pin_3, D19.A
  N28: S20.pin_3, D20.A
  N29: D17.C, D18.C, D19.C, D20.C, D21.C, Pro_Micro1.10
  GND: Pro_Micro1.GND, Grove1.GND
  N30: Pro_Micro1.2, Grove1.SDA
  N31: Pro_Micro1.3, Pro_Micro1.4, Grove1.SCL
  VCC: Pro_Micro1.VCC, Grove1.VCC

custom parts:
  SparkFun Pro Micro: The Pro Micro is similar to the Pro Mini except with an ATmega32U4 on board. The USB transceiver inside the 32U4 allows us to add USB connectivity on-board and do away with bulky external USB interface. Based on: https://github.com/unorthodox-engineers/unorthodox-arduino/blob/master/Unorthodox/fritzing/parts/Pro%20Micro.fzpz
